// Logisim project 16_Input_Parallel_Sort.circ as structural Verilog: 2 circuits, main circuit Bitonic_Merge_Sort
module Bitonic_Merge_Sort (
);

  wire CLK;
  wire [3:0] findmaxmin_1_max_of_a_b, findmaxmin_1_min_of_a_b, findmaxmin_2_max_of_a_b,
       findmaxmin_2_min_of_a_b, findmaxmin_3_max_of_a_b, findmaxmin_3_min_of_a_b, findmaxmin_4_max_of_a_b,
       findmaxmin_4_min_of_a_b, findmaxmin_5_max_of_a_b, findmaxmin_5_min_of_a_b, findmaxmin_6_max_of_a_b,
       findmaxmin_6_min_of_a_b, findmaxmin_7_max_of_a_b, findmaxmin_7_min_of_a_b, findmaxmin_8_max_of_a_b,
       findmaxmin_8_min_of_a_b, findmaxmin_9_max_of_a_b, findmaxmin_9_min_of_a_b, findmaxmin_10_max_of_a_b,
       findmaxmin_10_min_of_a_b, findmaxmin_11_max_of_a_b, findmaxmin_11_min_of_a_b,
       findmaxmin_12_max_of_a_b, findmaxmin_12_min_of_a_b, findmaxmin_13_max_of_a_b,
       findmaxmin_13_min_of_a_b, findmaxmin_14_max_of_a_b, findmaxmin_14_min_of_a_b,
       findmaxmin_15_max_of_a_b, findmaxmin_15_min_of_a_b, findmaxmin_16_max_of_a_b,
       findmaxmin_16_min_of_a_b, findmaxmin_17_max_of_a_b, findmaxmin_17_min_of_a_b,
       findmaxmin_18_max_of_a_b, findmaxmin_18_min_of_a_b, findmaxmin_19_max_of_a_b,
       findmaxmin_19_min_of_a_b, findmaxmin_20_max_of_a_b, findmaxmin_20_min_of_a_b,
       findmaxmin_21_max_of_a_b, findmaxmin_21_min_of_a_b, findmaxmin_22_max_of_a_b,
       findmaxmin_22_min_of_a_b, findmaxmin_23_max_of_a_b, findmaxmin_23_min_of_a_b,
       findmaxmin_24_max_of_a_b, findmaxmin_24_min_of_a_b, findmaxmin_25_max_of_a_b,
       findmaxmin_25_min_of_a_b, findmaxmin_26_max_of_a_b, findmaxmin_26_min_of_a_b,
       findmaxmin_27_max_of_a_b, findmaxmin_27_min_of_a_b, findmaxmin_28_max_of_a_b,
       findmaxmin_28_min_of_a_b, findmaxmin_29_max_of_a_b, findmaxmin_29_min_of_a_b,
       findmaxmin_30_max_of_a_b, findmaxmin_30_min_of_a_b, findmaxmin_31_max_of_a_b,
       findmaxmin_31_min_of_a_b, findmaxmin_32_max_of_a_b, findmaxmin_32_min_of_a_b,
       findmaxmin_33_max_of_a_b, findmaxmin_33_min_of_a_b, findmaxmin_34_max_of_a_b,
       findmaxmin_34_min_of_a_b, findmaxmin_35_max_of_a_b, findmaxmin_35_min_of_a_b,
       findmaxmin_36_max_of_a_b, findmaxmin_36_min_of_a_b, findmaxmin_37_max_of_a_b,
       findmaxmin_37_min_of_a_b, findmaxmin_38_max_of_a_b, findmaxmin_38_min_of_a_b,
       findmaxmin_39_max_of_a_b, findmaxmin_39_min_of_a_b, findmaxmin_40_max_of_a_b,
       findmaxmin_40_min_of_a_b, findmaxmin_41_max_of_a_b, findmaxmin_41_min_of_a_b,
       findmaxmin_42_max_of_a_b, findmaxmin_42_min_of_a_b, findmaxmin_43_max_of_a_b,
       findmaxmin_43_min_of_a_b, findmaxmin_44_max_of_a_b, findmaxmin_44_min_of_a_b,
       findmaxmin_45_max_of_a_b, findmaxmin_45_min_of_a_b, findmaxmin_46_max_of_a_b,
       findmaxmin_46_min_of_a_b, findmaxmin_47_max_of_a_b, findmaxmin_47_min_of_a_b,
       findmaxmin_48_max_of_a_b, findmaxmin_48_min_of_a_b, findmaxmin_49_max_of_a_b,
       findmaxmin_49_min_of_a_b, findmaxmin_50_max_of_a_b, findmaxmin_50_min_of_a_b,
       findmaxmin_51_max_of_a_b, findmaxmin_51_min_of_a_b, findmaxmin_52_max_of_a_b,
       findmaxmin_52_min_of_a_b, findmaxmin_53_max_of_a_b, findmaxmin_53_min_of_a_b,
       findmaxmin_54_max_of_a_b, findmaxmin_54_min_of_a_b, findmaxmin_55_max_of_a_b,
       findmaxmin_55_min_of_a_b, findmaxmin_56_max_of_a_b, findmaxmin_56_min_of_a_b,
       findmaxmin_57_max_of_a_b, findmaxmin_57_min_of_a_b, findmaxmin_58_max_of_a_b,
       findmaxmin_58_min_of_a_b, findmaxmin_59_max_of_a_b, findmaxmin_59_min_of_a_b,
       findmaxmin_60_max_of_a_b, findmaxmin_60_min_of_a_b, findmaxmin_61_max_of_a_b,
       findmaxmin_61_min_of_a_b, findmaxmin_62_max_of_a_b, findmaxmin_62_min_of_a_b,
       findmaxmin_63_max_of_a_b, findmaxmin_63_min_of_a_b, findmaxmin_64_max_of_a_b,
       findmaxmin_64_min_of_a_b, findmaxmin_65_max_of_a_b, findmaxmin_65_min_of_a_b,
       findmaxmin_66_max_of_a_b, findmaxmin_66_min_of_a_b, findmaxmin_67_max_of_a_b,
       findmaxmin_67_min_of_a_b, findmaxmin_68_max_of_a_b, findmaxmin_68_min_of_a_b,
       findmaxmin_69_max_of_a_b, findmaxmin_69_min_of_a_b, findmaxmin_70_max_of_a_b,
       findmaxmin_70_min_of_a_b, findmaxmin_71_max_of_a_b, findmaxmin_71_min_of_a_b,
       findmaxmin_72_max_of_a_b, findmaxmin_72_min_of_a_b, findmaxmin_73_max_of_a_b,
       findmaxmin_73_min_of_a_b, findmaxmin_74_max_of_a_b, findmaxmin_74_min_of_a_b,
       findmaxmin_75_max_of_a_b, findmaxmin_75_min_of_a_b, findmaxmin_76_max_of_a_b,
       findmaxmin_76_min_of_a_b, findmaxmin_77_max_of_a_b, findmaxmin_77_min_of_a_b,
       findmaxmin_78_max_of_a_b, findmaxmin_78_min_of_a_b, findmaxmin_79_max_of_a_b,
       findmaxmin_79_min_of_a_b, findmaxmin_80_max_of_a_b, findmaxmin_80_min_of_a_b, random_1_out,
       random_2_out, random_3_out, random_4_out, random_5_out, random_6_out, random_7_out, random_8_out,
       random_9_out, random_10_out, random_11_out, random_12_out, random_13_out, random_14_out,
       random_15_out, random_16_out, register_1_q, register_2_q, register_3_q, register_4_q, register_5_q,
       register_6_q, register_7_q, register_8_q, register_9_q, register_10_q, register_11_q, register_12_q,
       register_13_q, register_14_q, register_15_q, register_16_q;

  Clock clock_1 (.out(CLK));
  Random #(.width(4)) random_1 (.clk(CLK), .out(random_1_out));  // open: clr, next
  Random #(.width(4)) random_2 (.clk(CLK), .out(random_2_out));  // open: clr, next
  Random #(.width(4)) random_3 (.clk(CLK), .out(random_3_out));  // open: clr, next
  Random #(.width(4)) random_4 (.clk(CLK), .out(random_4_out));  // open: clr, next
  Random #(.width(4)) random_5 (.clk(CLK), .out(random_5_out));  // open: clr, next
  Random #(.width(4)) random_6 (.clk(CLK), .out(random_6_out));  // open: clr, next
  Random #(.width(4)) random_7 (.clk(CLK), .out(random_7_out));  // open: clr, next
  Random #(.width(4)) random_8 (.clk(CLK), .out(random_8_out));  // open: clr, next
  Random #(.width(4)) random_9 (.clk(CLK), .out(random_9_out));  // open: clr, next
  Random #(.width(4)) random_10 (.clk(CLK), .out(random_10_out));  // open: clr, next
  Random #(.width(4)) random_11 (.clk(CLK), .out(random_11_out));  // open: clr, next
  Random #(.width(4)) random_12 (.clk(CLK), .out(random_12_out));  // open: clr, next
  Random #(.width(4)) random_13 (.clk(CLK), .out(random_13_out));  // open: clr, next
  Random #(.width(4)) random_14 (.clk(CLK), .out(random_14_out));  // open: clr, next
  Random #(.width(4)) random_15 (.clk(CLK), .out(random_15_out));  // open: clr, next
  Random #(.width(4)) random_16 (.clk(CLK), .out(random_16_out));  // open: clr, next
  FindMaxMin findmaxmin_1 (
    .A(random_1_out), .B(random_2_out), .Max_of_A_B(findmaxmin_1_max_of_a_b),
    .Min_of_A_B(findmaxmin_1_min_of_a_b));
  FindMaxMin findmaxmin_2 (
    .A(random_3_out), .B(random_4_out), .Max_of_A_B(findmaxmin_2_max_of_a_b),
    .Min_of_A_B(findmaxmin_2_min_of_a_b));
  FindMaxMin findmaxmin_3 (
    .A(random_5_out), .B(random_6_out), .Max_of_A_B(findmaxmin_3_max_of_a_b),
    .Min_of_A_B(findmaxmin_3_min_of_a_b));
  FindMaxMin findmaxmin_4 (
    .A(random_7_out), .B(random_8_out), .Max_of_A_B(findmaxmin_4_max_of_a_b),
    .Min_of_A_B(findmaxmin_4_min_of_a_b));
  FindMaxMin findmaxmin_5 (
    .A(random_9_out), .B(random_10_out), .Max_of_A_B(findmaxmin_5_max_of_a_b),
    .Min_of_A_B(findmaxmin_5_min_of_a_b));
  FindMaxMin findmaxmin_6 (
    .A(random_11_out), .B(random_12_out), .Max_of_A_B(findmaxmin_6_max_of_a_b),
    .Min_of_A_B(findmaxmin_6_min_of_a_b));
  FindMaxMin findmaxmin_7 (
    .A(random_13_out), .B(random_14_out), .Max_of_A_B(findmaxmin_7_max_of_a_b),
    .Min_of_A_B(findmaxmin_7_min_of_a_b));
  FindMaxMin findmaxmin_8 (
    .A(random_15_out), .B(random_16_out), .Max_of_A_B(findmaxmin_8_max_of_a_b),
    .Min_of_A_B(findmaxmin_8_min_of_a_b));
  FindMaxMin findmaxmin_9 (
    .A(findmaxmin_1_max_of_a_b), .B(findmaxmin_2_min_of_a_b), .Max_of_A_B(findmaxmin_9_max_of_a_b),
    .Min_of_A_B(findmaxmin_9_min_of_a_b));
  FindMaxMin findmaxmin_10 (
    .A(findmaxmin_1_min_of_a_b), .B(findmaxmin_2_max_of_a_b), .Max_of_A_B(findmaxmin_10_max_of_a_b),
    .Min_of_A_B(findmaxmin_10_min_of_a_b));
  FindMaxMin findmaxmin_11 (
    .A(findmaxmin_3_max_of_a_b), .B(findmaxmin_4_min_of_a_b), .Max_of_A_B(findmaxmin_11_max_of_a_b),
    .Min_of_A_B(findmaxmin_11_min_of_a_b));
  FindMaxMin findmaxmin_12 (
    .A(findmaxmin_3_min_of_a_b), .B(findmaxmin_4_max_of_a_b), .Max_of_A_B(findmaxmin_12_max_of_a_b),
    .Min_of_A_B(findmaxmin_12_min_of_a_b));
  FindMaxMin findmaxmin_13 (
    .A(findmaxmin_5_max_of_a_b), .B(findmaxmin_6_min_of_a_b), .Max_of_A_B(findmaxmin_13_max_of_a_b),
    .Min_of_A_B(findmaxmin_13_min_of_a_b));
  FindMaxMin findmaxmin_14 (
    .A(findmaxmin_5_min_of_a_b), .B(findmaxmin_6_max_of_a_b), .Max_of_A_B(findmaxmin_14_max_of_a_b),
    .Min_of_A_B(findmaxmin_14_min_of_a_b));
  FindMaxMin findmaxmin_15 (
    .A(findmaxmin_7_max_of_a_b), .B(findmaxmin_8_min_of_a_b), .Max_of_A_B(findmaxmin_15_max_of_a_b),
    .Min_of_A_B(findmaxmin_15_min_of_a_b));
  FindMaxMin findmaxmin_16 (
    .A(findmaxmin_7_min_of_a_b), .B(findmaxmin_8_max_of_a_b), .Max_of_A_B(findmaxmin_16_max_of_a_b),
    .Min_of_A_B(findmaxmin_16_min_of_a_b));
  FindMaxMin findmaxmin_17 (
    .A(findmaxmin_9_max_of_a_b), .B(findmaxmin_10_max_of_a_b), .Max_of_A_B(findmaxmin_17_max_of_a_b),
    .Min_of_A_B(findmaxmin_17_min_of_a_b));
  FindMaxMin findmaxmin_18 (
    .A(findmaxmin_9_min_of_a_b), .B(findmaxmin_10_min_of_a_b), .Max_of_A_B(findmaxmin_18_max_of_a_b),
    .Min_of_A_B(findmaxmin_18_min_of_a_b));
  FindMaxMin findmaxmin_19 (
    .A(findmaxmin_11_max_of_a_b), .B(findmaxmin_12_max_of_a_b), .Max_of_A_B(findmaxmin_19_max_of_a_b),
    .Min_of_A_B(findmaxmin_19_min_of_a_b));
  FindMaxMin findmaxmin_20 (
    .A(findmaxmin_11_min_of_a_b), .B(findmaxmin_12_min_of_a_b), .Max_of_A_B(findmaxmin_20_max_of_a_b),
    .Min_of_A_B(findmaxmin_20_min_of_a_b));
  FindMaxMin findmaxmin_21 (
    .A(findmaxmin_13_max_of_a_b), .B(findmaxmin_14_max_of_a_b), .Max_of_A_B(findmaxmin_21_max_of_a_b),
    .Min_of_A_B(findmaxmin_21_min_of_a_b));
  FindMaxMin findmaxmin_22 (
    .A(findmaxmin_13_min_of_a_b), .B(findmaxmin_14_min_of_a_b), .Max_of_A_B(findmaxmin_22_max_of_a_b),
    .Min_of_A_B(findmaxmin_22_min_of_a_b));
  FindMaxMin findmaxmin_23 (
    .A(findmaxmin_15_max_of_a_b), .B(findmaxmin_16_max_of_a_b), .Max_of_A_B(findmaxmin_23_max_of_a_b),
    .Min_of_A_B(findmaxmin_23_min_of_a_b));
  FindMaxMin findmaxmin_24 (
    .A(findmaxmin_15_min_of_a_b), .B(findmaxmin_16_min_of_a_b), .Max_of_A_B(findmaxmin_24_max_of_a_b),
    .Min_of_A_B(findmaxmin_24_min_of_a_b));
  FindMaxMin findmaxmin_25 (
    .A(findmaxmin_18_min_of_a_b), .B(findmaxmin_19_max_of_a_b), .Max_of_A_B(findmaxmin_25_max_of_a_b),
    .Min_of_A_B(findmaxmin_25_min_of_a_b));
  FindMaxMin findmaxmin_26 (
    .A(findmaxmin_19_min_of_a_b), .B(findmaxmin_18_max_of_a_b), .Max_of_A_B(findmaxmin_26_max_of_a_b),
    .Min_of_A_B(findmaxmin_26_min_of_a_b));
  FindMaxMin findmaxmin_27 (
    .A(findmaxmin_17_min_of_a_b), .B(findmaxmin_20_max_of_a_b), .Max_of_A_B(findmaxmin_27_max_of_a_b),
    .Min_of_A_B(findmaxmin_27_min_of_a_b));
  FindMaxMin findmaxmin_28 (
    .A(findmaxmin_17_max_of_a_b), .B(findmaxmin_20_min_of_a_b), .Max_of_A_B(findmaxmin_28_max_of_a_b),
    .Min_of_A_B(findmaxmin_28_min_of_a_b));
  FindMaxMin findmaxmin_29 (
    .A(findmaxmin_22_min_of_a_b), .B(findmaxmin_23_max_of_a_b), .Max_of_A_B(findmaxmin_29_max_of_a_b),
    .Min_of_A_B(findmaxmin_29_min_of_a_b));
  FindMaxMin findmaxmin_30 (
    .A(findmaxmin_23_min_of_a_b), .B(findmaxmin_22_max_of_a_b), .Max_of_A_B(findmaxmin_30_max_of_a_b),
    .Min_of_A_B(findmaxmin_30_min_of_a_b));
  FindMaxMin findmaxmin_31 (
    .A(findmaxmin_21_min_of_a_b), .B(findmaxmin_24_max_of_a_b), .Max_of_A_B(findmaxmin_31_max_of_a_b),
    .Min_of_A_B(findmaxmin_31_min_of_a_b));
  FindMaxMin findmaxmin_32 (
    .A(findmaxmin_21_max_of_a_b), .B(findmaxmin_24_min_of_a_b), .Max_of_A_B(findmaxmin_32_max_of_a_b),
    .Min_of_A_B(findmaxmin_32_min_of_a_b));
  FindMaxMin findmaxmin_33 (
    .A(findmaxmin_25_min_of_a_b), .B(findmaxmin_27_min_of_a_b), .Max_of_A_B(findmaxmin_33_max_of_a_b),
    .Min_of_A_B(findmaxmin_33_min_of_a_b));
  FindMaxMin findmaxmin_34 (
    .A(findmaxmin_26_min_of_a_b), .B(findmaxmin_28_min_of_a_b), .Max_of_A_B(findmaxmin_34_max_of_a_b),
    .Min_of_A_B(findmaxmin_34_min_of_a_b));
  FindMaxMin findmaxmin_35 (
    .A(findmaxmin_25_max_of_a_b), .B(findmaxmin_27_max_of_a_b), .Max_of_A_B(findmaxmin_35_max_of_a_b),
    .Min_of_A_B(findmaxmin_35_min_of_a_b));
  FindMaxMin findmaxmin_36 (
    .A(findmaxmin_26_max_of_a_b), .B(findmaxmin_28_max_of_a_b), .Max_of_A_B(findmaxmin_36_max_of_a_b),
    .Min_of_A_B(findmaxmin_36_min_of_a_b));
  FindMaxMin findmaxmin_37 (
    .A(findmaxmin_29_min_of_a_b), .B(findmaxmin_31_min_of_a_b), .Max_of_A_B(findmaxmin_37_max_of_a_b),
    .Min_of_A_B(findmaxmin_37_min_of_a_b));
  FindMaxMin findmaxmin_38 (
    .A(findmaxmin_30_min_of_a_b), .B(findmaxmin_32_min_of_a_b), .Max_of_A_B(findmaxmin_38_max_of_a_b),
    .Min_of_A_B(findmaxmin_38_min_of_a_b));
  FindMaxMin findmaxmin_39 (
    .A(findmaxmin_29_max_of_a_b), .B(findmaxmin_31_max_of_a_b), .Max_of_A_B(findmaxmin_39_max_of_a_b),
    .Min_of_A_B(findmaxmin_39_min_of_a_b));
  FindMaxMin findmaxmin_40 (
    .A(findmaxmin_30_max_of_a_b), .B(findmaxmin_32_max_of_a_b), .Max_of_A_B(findmaxmin_40_max_of_a_b),
    .Min_of_A_B(findmaxmin_40_min_of_a_b));
  FindMaxMin findmaxmin_41 (
    .A(findmaxmin_33_min_of_a_b), .B(findmaxmin_34_min_of_a_b), .Max_of_A_B(findmaxmin_41_max_of_a_b),
    .Min_of_A_B(findmaxmin_41_min_of_a_b));
  FindMaxMin findmaxmin_42 (
    .A(findmaxmin_37_min_of_a_b), .B(findmaxmin_38_min_of_a_b), .Max_of_A_B(findmaxmin_42_max_of_a_b),
    .Min_of_A_B(findmaxmin_42_min_of_a_b));
  FindMaxMin findmaxmin_43 (
    .A(findmaxmin_33_max_of_a_b), .B(findmaxmin_34_max_of_a_b), .Max_of_A_B(findmaxmin_43_max_of_a_b),
    .Min_of_A_B(findmaxmin_43_min_of_a_b));
  FindMaxMin findmaxmin_44 (
    .A(findmaxmin_35_min_of_a_b), .B(findmaxmin_36_min_of_a_b), .Max_of_A_B(findmaxmin_44_max_of_a_b),
    .Min_of_A_B(findmaxmin_44_min_of_a_b));
  FindMaxMin findmaxmin_45 (
    .A(findmaxmin_35_max_of_a_b), .B(findmaxmin_36_max_of_a_b), .Max_of_A_B(findmaxmin_45_max_of_a_b),
    .Min_of_A_B(findmaxmin_45_min_of_a_b));
  FindMaxMin findmaxmin_46 (
    .A(findmaxmin_37_max_of_a_b), .B(findmaxmin_38_max_of_a_b), .Max_of_A_B(findmaxmin_46_max_of_a_b),
    .Min_of_A_B(findmaxmin_46_min_of_a_b));
  FindMaxMin findmaxmin_47 (
    .A(findmaxmin_39_min_of_a_b), .B(findmaxmin_40_min_of_a_b), .Max_of_A_B(findmaxmin_47_max_of_a_b),
    .Min_of_A_B(findmaxmin_47_min_of_a_b));
  FindMaxMin findmaxmin_48 (
    .A(findmaxmin_39_max_of_a_b), .B(findmaxmin_40_max_of_a_b), .Max_of_A_B(findmaxmin_48_max_of_a_b),
    .Min_of_A_B(findmaxmin_48_min_of_a_b));
  FindMaxMin findmaxmin_49 (
    .A(findmaxmin_41_min_of_a_b), .B(findmaxmin_48_max_of_a_b), .Max_of_A_B(findmaxmin_49_max_of_a_b),
    .Min_of_A_B(findmaxmin_49_min_of_a_b));
  FindMaxMin findmaxmin_50 (
    .A(findmaxmin_41_max_of_a_b), .B(findmaxmin_48_min_of_a_b), .Max_of_A_B(findmaxmin_50_max_of_a_b),
    .Min_of_A_B(findmaxmin_50_min_of_a_b));
  FindMaxMin findmaxmin_51 (
    .A(findmaxmin_43_min_of_a_b), .B(findmaxmin_47_max_of_a_b), .Max_of_A_B(findmaxmin_51_max_of_a_b),
    .Min_of_A_B(findmaxmin_51_min_of_a_b));
  FindMaxMin findmaxmin_52 (
    .A(findmaxmin_43_max_of_a_b), .B(findmaxmin_47_min_of_a_b), .Max_of_A_B(findmaxmin_52_max_of_a_b),
    .Min_of_A_B(findmaxmin_52_min_of_a_b));
  FindMaxMin findmaxmin_53 (
    .A(findmaxmin_44_min_of_a_b), .B(findmaxmin_46_max_of_a_b), .Max_of_A_B(findmaxmin_53_max_of_a_b),
    .Min_of_A_B(findmaxmin_53_min_of_a_b));
  FindMaxMin findmaxmin_54 (
    .A(findmaxmin_44_max_of_a_b), .B(findmaxmin_46_min_of_a_b), .Max_of_A_B(findmaxmin_54_max_of_a_b),
    .Min_of_A_B(findmaxmin_54_min_of_a_b));
  FindMaxMin findmaxmin_55 (
    .A(findmaxmin_45_min_of_a_b), .B(findmaxmin_42_max_of_a_b), .Max_of_A_B(findmaxmin_55_max_of_a_b),
    .Min_of_A_B(findmaxmin_55_min_of_a_b));
  FindMaxMin findmaxmin_56 (
    .A(findmaxmin_45_max_of_a_b), .B(findmaxmin_42_min_of_a_b), .Max_of_A_B(findmaxmin_56_max_of_a_b),
    .Min_of_A_B(findmaxmin_56_min_of_a_b));
  FindMaxMin findmaxmin_57 (
    .A(findmaxmin_49_min_of_a_b), .B(findmaxmin_53_min_of_a_b), .Max_of_A_B(findmaxmin_57_max_of_a_b),
    .Min_of_A_B(findmaxmin_57_min_of_a_b));
  FindMaxMin findmaxmin_58 (
    .A(findmaxmin_50_min_of_a_b), .B(findmaxmin_54_min_of_a_b), .Max_of_A_B(findmaxmin_58_max_of_a_b),
    .Min_of_A_B(findmaxmin_58_min_of_a_b));
  FindMaxMin findmaxmin_59 (
    .A(findmaxmin_51_min_of_a_b), .B(findmaxmin_55_min_of_a_b), .Max_of_A_B(findmaxmin_59_max_of_a_b),
    .Min_of_A_B(findmaxmin_59_min_of_a_b));
  FindMaxMin findmaxmin_60 (
    .A(findmaxmin_52_min_of_a_b), .B(findmaxmin_56_min_of_a_b), .Max_of_A_B(findmaxmin_60_max_of_a_b),
    .Min_of_A_B(findmaxmin_60_min_of_a_b));
  FindMaxMin findmaxmin_61 (
    .A(findmaxmin_49_max_of_a_b), .B(findmaxmin_53_max_of_a_b), .Max_of_A_B(findmaxmin_61_max_of_a_b),
    .Min_of_A_B(findmaxmin_61_min_of_a_b));
  FindMaxMin findmaxmin_62 (
    .A(findmaxmin_50_max_of_a_b), .B(findmaxmin_54_max_of_a_b), .Max_of_A_B(findmaxmin_62_max_of_a_b),
    .Min_of_A_B(findmaxmin_62_min_of_a_b));
  FindMaxMin findmaxmin_63 (
    .A(findmaxmin_51_max_of_a_b), .B(findmaxmin_55_max_of_a_b), .Max_of_A_B(findmaxmin_63_max_of_a_b),
    .Min_of_A_B(findmaxmin_63_min_of_a_b));
  FindMaxMin findmaxmin_64 (
    .A(findmaxmin_52_max_of_a_b), .B(findmaxmin_56_max_of_a_b), .Max_of_A_B(findmaxmin_64_max_of_a_b),
    .Min_of_A_B(findmaxmin_64_min_of_a_b));
  FindMaxMin findmaxmin_65 (
    .A(findmaxmin_57_min_of_a_b), .B(findmaxmin_59_min_of_a_b), .Max_of_A_B(findmaxmin_65_max_of_a_b),
    .Min_of_A_B(findmaxmin_65_min_of_a_b));
  FindMaxMin findmaxmin_66 (
    .A(findmaxmin_58_min_of_a_b), .B(findmaxmin_60_min_of_a_b), .Max_of_A_B(findmaxmin_66_max_of_a_b),
    .Min_of_A_B(findmaxmin_66_min_of_a_b));
  FindMaxMin findmaxmin_67 (
    .A(findmaxmin_57_max_of_a_b), .B(findmaxmin_59_max_of_a_b), .Max_of_A_B(findmaxmin_67_max_of_a_b),
    .Min_of_A_B(findmaxmin_67_min_of_a_b));
  FindMaxMin findmaxmin_68 (
    .A(findmaxmin_58_max_of_a_b), .B(findmaxmin_60_max_of_a_b), .Max_of_A_B(findmaxmin_68_max_of_a_b),
    .Min_of_A_B(findmaxmin_68_min_of_a_b));
  FindMaxMin findmaxmin_69 (
    .A(findmaxmin_61_min_of_a_b), .B(findmaxmin_63_min_of_a_b), .Max_of_A_B(findmaxmin_69_max_of_a_b),
    .Min_of_A_B(findmaxmin_69_min_of_a_b));
  FindMaxMin findmaxmin_70 (
    .A(findmaxmin_62_min_of_a_b), .B(findmaxmin_64_min_of_a_b), .Max_of_A_B(findmaxmin_70_max_of_a_b),
    .Min_of_A_B(findmaxmin_70_min_of_a_b));
  FindMaxMin findmaxmin_71 (
    .A(findmaxmin_61_max_of_a_b), .B(findmaxmin_63_max_of_a_b), .Max_of_A_B(findmaxmin_71_max_of_a_b),
    .Min_of_A_B(findmaxmin_71_min_of_a_b));
  FindMaxMin findmaxmin_72 (
    .A(findmaxmin_62_max_of_a_b), .B(findmaxmin_64_max_of_a_b), .Max_of_A_B(findmaxmin_72_max_of_a_b),
    .Min_of_A_B(findmaxmin_72_min_of_a_b));
  FindMaxMin findmaxmin_73 (
    .A(findmaxmin_65_min_of_a_b), .B(findmaxmin_66_min_of_a_b), .Max_of_A_B(findmaxmin_73_max_of_a_b),
    .Min_of_A_B(findmaxmin_73_min_of_a_b));
  FindMaxMin findmaxmin_74 (
    .A(findmaxmin_65_max_of_a_b), .B(findmaxmin_66_max_of_a_b), .Max_of_A_B(findmaxmin_74_max_of_a_b),
    .Min_of_A_B(findmaxmin_74_min_of_a_b));
  FindMaxMin findmaxmin_75 (
    .A(findmaxmin_67_min_of_a_b), .B(findmaxmin_68_min_of_a_b), .Max_of_A_B(findmaxmin_75_max_of_a_b),
    .Min_of_A_B(findmaxmin_75_min_of_a_b));
  FindMaxMin findmaxmin_76 (
    .A(findmaxmin_67_max_of_a_b), .B(findmaxmin_68_max_of_a_b), .Max_of_A_B(findmaxmin_76_max_of_a_b),
    .Min_of_A_B(findmaxmin_76_min_of_a_b));
  FindMaxMin findmaxmin_77 (
    .A(findmaxmin_69_min_of_a_b), .B(findmaxmin_70_min_of_a_b), .Max_of_A_B(findmaxmin_77_max_of_a_b),
    .Min_of_A_B(findmaxmin_77_min_of_a_b));
  FindMaxMin findmaxmin_78 (
    .A(findmaxmin_69_max_of_a_b), .B(findmaxmin_70_max_of_a_b), .Max_of_A_B(findmaxmin_78_max_of_a_b),
    .Min_of_A_B(findmaxmin_78_min_of_a_b));
  FindMaxMin findmaxmin_79 (
    .A(findmaxmin_71_min_of_a_b), .B(findmaxmin_72_min_of_a_b), .Max_of_A_B(findmaxmin_79_max_of_a_b),
    .Min_of_A_B(findmaxmin_79_min_of_a_b));
  FindMaxMin findmaxmin_80 (
    .A(findmaxmin_71_max_of_a_b), .B(findmaxmin_72_max_of_a_b), .Max_of_A_B(findmaxmin_80_max_of_a_b),
    .Min_of_A_B(findmaxmin_80_min_of_a_b));
  Register #(.width(4)) register_1 (.D(findmaxmin_73_min_of_a_b), .clk(CLK), .Q(register_1_q));  // open: en, clr
  Register #(.width(4)) register_2 (.D(findmaxmin_73_max_of_a_b), .clk(CLK), .Q(register_2_q));  // open: en, clr
  Register #(.width(4)) register_3 (.D(findmaxmin_74_min_of_a_b), .clk(CLK), .Q(register_3_q));  // open: en, clr
  Register #(.width(4)) register_4 (.D(findmaxmin_74_max_of_a_b), .clk(CLK), .Q(register_4_q));  // open: en, clr
  Register #(.width(4)) register_5 (.D(findmaxmin_75_min_of_a_b), .clk(CLK), .Q(register_5_q));  // open: en, clr
  Register #(.width(4)) register_6 (.D(findmaxmin_75_max_of_a_b), .clk(CLK), .Q(register_6_q));  // open: en, clr
  Register #(.width(4)) register_7 (.D(findmaxmin_76_min_of_a_b), .clk(CLK), .Q(register_7_q));  // open: en, clr
  Register #(.width(4)) register_8 (.D(findmaxmin_76_max_of_a_b), .clk(CLK), .Q(register_8_q));  // open: en, clr
  Register #(.width(4)) register_9 (.D(findmaxmin_77_min_of_a_b), .clk(CLK), .Q(register_9_q));  // open: en, clr
  Register #(.width(4)) register_10 (.D(findmaxmin_77_max_of_a_b), .clk(CLK), .Q(register_10_q));  // open: en, clr
  Register #(.width(4)) register_11 (.D(findmaxmin_78_min_of_a_b), .clk(CLK), .Q(register_11_q));  // open: en, clr
  Register #(.width(4)) register_12 (.D(findmaxmin_78_max_of_a_b), .clk(CLK), .Q(register_12_q));  // open: en, clr
  Register #(.width(4)) register_13 (.D(findmaxmin_79_min_of_a_b), .clk(CLK), .Q(register_13_q));  // open: en, clr
  Register #(.width(4)) register_14 (.D(findmaxmin_79_max_of_a_b), .clk(CLK), .Q(register_14_q));  // open: en, clr
  Register #(.width(4)) register_15 (.D(findmaxmin_80_min_of_a_b), .clk(CLK), .Q(register_15_q));  // open: en, clr
  Register #(.width(4)) register_16 (.D(findmaxmin_80_max_of_a_b), .clk(CLK), .Q(register_16_q));  // open: en, clr
  Hex_Digit_Display hex_digit_display_1 (.value(register_1_q));  // open: dp
  Hex_Digit_Display hex_digit_display_2 (.value(register_2_q));  // open: dp
  Hex_Digit_Display hex_digit_display_3 (.value(register_3_q));  // open: dp
  Hex_Digit_Display hex_digit_display_4 (.value(register_4_q));  // open: dp
  Hex_Digit_Display hex_digit_display_5 (.value(register_5_q));  // open: dp
  Hex_Digit_Display hex_digit_display_6 (.value(register_6_q));  // open: dp
  Hex_Digit_Display hex_digit_display_7 (.value(register_7_q));  // open: dp
  Hex_Digit_Display hex_digit_display_8 (.value(register_8_q));  // open: dp
  Hex_Digit_Display hex_digit_display_9 (.value(register_9_q));  // open: dp
  Hex_Digit_Display hex_digit_display_10 (.value(register_10_q));  // open: dp
  Hex_Digit_Display hex_digit_display_11 (.value(register_11_q));  // open: dp
  Hex_Digit_Display hex_digit_display_12 (.value(register_12_q));  // open: dp
  Hex_Digit_Display hex_digit_display_13 (.value(register_13_q));  // open: dp
  Hex_Digit_Display hex_digit_display_14 (.value(register_14_q));  // open: dp
  Hex_Digit_Display hex_digit_display_15 (.value(register_15_q));  // open: dp
  Hex_Digit_Display hex_digit_display_16 (.value(register_16_q));  // open: dp
endmodule

module FindMaxMin (
  input  [3:0] A,
  input  [3:0] B,
  output [3:0] Max_of_A_B,
  output [3:0] Min_of_A_B
);

  wire comparator_1_gt;

  Multiplexer #(.width(4)) multiplexer_1 (.in1(B), .out(Min_of_A_B), .sel(comparator_1_gt));  // open: in0
  Comparator #(.mode("unsigned"), .width(4)) comparator_1 (.a(A), .b(B), .gt(comparator_1_gt));  // open: eq, lt
  Multiplexer #(.width(4)) multiplexer_2 (.in1(A), .out(Max_of_A_B), .sel(comparator_1_gt));  // open: in0
  Multiplexer #(.width(4)) multiplexer_3 (.in0(B), .out(Max_of_A_B), .sel(comparator_1_gt));  // open: in1
  Multiplexer #(.width(4)) multiplexer_4 (.in0(A), .out(Min_of_A_B), .sel(comparator_1_gt));  // open: in1
endmodule
